// Logisim project register.circ as structural Verilog: 1 circuit, main circuit main
module main (
  input  [15:0] in_1
);

  D_Flip_Flop d_ff_1 (.D(in_1[0]));  // open: clk, Q, Qn, preset, en, reset
  D_Flip_Flop d_ff_2 (.D(in_1[8]));  // open: clk, Q, Qn, preset, en, reset
  D_Flip_Flop d_ff_3 (.D(in_1[1]));  // open: clk, Q, Qn, preset, en, reset
  D_Flip_Flop d_ff_4 (.D(in_1[9]));  // open: clk, Q, Qn, preset, en, reset
  D_Flip_Flop d_ff_5 ();  // open: clk, D, Q, Qn, preset, en, reset
  D_Flip_Flop d_ff_6 (.D(in_1[10]));  // open: clk, Q, Qn, preset, en, reset
  D_Flip_Flop d_ff_7 (.D(in_1[3]));  // open: clk, Q, Qn, preset, en, reset
  D_Flip_Flop d_ff_8 (.D(in_1[11]));  // open: clk, Q, Qn, preset, en, reset
  D_Flip_Flop d_ff_9 (.D(in_1[4]));  // open: clk, Q, Qn, preset, en, reset
  D_Flip_Flop d_ff_10 (.D(in_1[12]));  // open: clk, Q, Qn, preset, en, reset
  D_Flip_Flop d_ff_11 (.D(in_1[5]));  // open: clk, Q, Qn, preset, en, reset
  D_Flip_Flop d_ff_12 (.D(in_1[13]));  // open: clk, Q, Qn, preset, en, reset
  D_Flip_Flop d_ff_13 (.D(in_1[6]));  // open: clk, Q, Qn, preset, en, reset
  D_Flip_Flop d_ff_14 (.D(in_1[14]));  // open: clk, Q, Qn, preset, en, reset
  D_Flip_Flop d_ff_15 (.D(in_1[7]));  // open: clk, Q, Qn, preset, en, reset
  D_Flip_Flop d_ff_16 (.D(in_1[15]));  // open: clk, Q, Qn, preset, en, reset

  // Other names for the same wires on the sheet: _0 = in_1[0]; _1 = in_1[1]; _2 = in_1[2]; _3 = in_1[3]; _4 = in_1[4];
  //   _5 = in_1[5]; _6 = in_1[6]; _7 = in_1[7]; _8 = in_1[8]; _9 = in_1[9]; _10 = in_1[10]; _11 = in_1[11];
  //   _12 = in_1[12]; _13 = in_1[13]; _14 = in_1[14]; _15 = in_1[15]
endmodule
